// Logisim project braille.circ as structural Verilog: 1 circuit, main circuit main
module main (
  input  in_1,
  input  in_2,
  input  [7:0] in_3,
  input  [4:0] _11111,
  input  in_5,
  input  in_6,
  input  in_7,
  output out_8,
  output out_9
);

  wire buffer_1_out, buffer_2_out, buffer_3_out, buffer_4_out, clock_1_out;
  wire [4:0] adder_1_out, rom_2_data;
  wire [5:0] rom_3_data;
  wire [7:0] counter_1_q, rom_1_data;

  Clock clock_1 (.out(clock_1_out));
  buf buffer_1 (buffer_1_out, clock_1_out);
  Counter counter_1 (
    .load(in_1), .D(in_3), .count(in_5), .Q(counter_1_q), .carry(out_8), .clk(buffer_1_out), .clr(in_6));
  buf buffer_2 (buffer_2_out, clock_1_out);
  ROM rom_1 (.addr(counter_1_q), .data(rom_1_data), .sel(buffer_2_out));
  buf buffer_3 (buffer_3_out, clock_1_out);
  ROM #(.dataWidth(5)) rom_2 (.addr(rom_1_data), .data(rom_2_data), .sel(buffer_3_out));
  Adder #(.width(5)) adder_1 (.a(rom_2_data), .b(_11111), .out(adder_1_out), .cin(in_2), .cout(out_9));
  buf buffer_4 (buffer_4_out, clock_1_out);
  ROM #(.addrWidth(5), .dataWidth(7)) rom_3 (.addr(adder_1_out), .data({in_7, rom_3_data}), .sel(buffer_4_out));
  LED led_1 (.in(rom_3_data[3]));
  LED led_2 (.in(rom_3_data[0]));
  LED led_3 (.in(rom_3_data[1]));
  LED led_4 (.in(rom_3_data[4]));
  LED led_5 (.in(rom_3_data[2]));
  LED led_6 (.in(rom_3_data[5]));

  // Notes on the sheet:
  //   Clock
  //   Contador
  //   1 - ativa a contagem
  //   1 - reinicia do 0
  //   insert
  //   contents of rom_1 (hex, n*v repeats v):
  //   61 62 63 64 65 66 67 68 69 6a 6c 6d 6e 6f 70 71 72 73 74 75 76 78 79 7a
  //   Tabela asc
  //   contents of rom_2 (hex, n*v repeats v):
  //   0 1 2 3 4 5 6 7 8 9 a b c d e f 10 11 12 13 14 15 16 17 18 19 1a 1b 1c 1d 1e 1f 0 1 2 3 4 5 6 7 8 9
  //   a b c d e f 10 11 12 13 14 15 16 17 18 19 1a 1b 1c 1d 1e 1f 0 1 2 3 4 5 6 7 8 9 a b c d e f 10 11 12
  //   13 14 15 16 17 18 19 1a 1b 1c 1d 1e 1f 0 1 2 3 4 5 6 7 8 9 a b c d e f 10 11 12 13 14 15 16 17 18 19
  //   1a 1b 1c 1d 1e 1f 0 1 2 3 4 5 6 7 8 9 a b c d e f 10 11 12 13 14 15 16 17 18 19 1a 1b 1c 1d 1e 1f 0
  //   1 2 3 4 5 6 7 8 9 a b c d e f 10 11 12 13 14 15 16 17 18 19 1a 1b 1c 1d 1e 1f 0 1 2 3 4 5 6 7 8 9 a
  //   b c d e f 10 11 12 13 14 15 16 17 18 19 1a 1b 1c 1d 1e 1f 0 1 2 3 4 5 6 7 8 9 a b c d e f 10 11 12
  //   13 14 15 16 17 18 19 1a 1b 1c 1d 1e
  //   Somador para inserir a partir do 0
  //   asc/braile
  //   contents of rom_3 (hex, n*v repeats v):
  //   1 3 9 19 11 b 1b 13 a 1a 5 7 d 1d 15 f 1f 17 e 1e 25 27 3a 2d 3d 35
  //   Braille
endmodule
