// Logisim project trabs.circ as structural Verilog: 1 circuit, main circuit main
module main (
  input  [7:0] in_1,
  input  [7:0] in_2,
  input  [7:0] in_3,
  input  [7:0] in_4,
  input  [7:0] in_5,
  input  [7:0] in_6,
  input  [7:0] _1000,
  input  [7:0] in_8,
  input  [7:0] _100,
  input  [7:0] _1001,
  input  [7:0] _110,
  input  [7:0] _1101,
  input  [2:0] in_13,
  input  \_1_grava_0_lê ,
  input  in_15,
  input  [2:0] in_16,
  input  [7:0] in_17,
  input  _1_acrescenta,
  input  in_19,
  input  volta_para_o_0,
  input  in_21
);

  wire controlled_inverter_1_out, not_1_out;
  wire [6:0] rom_1_data;
  wire [7:0] adder_1_out, adder_2_out, adder_3_out, adder_4_out, adder_5_out, controlled_buffer_1_out,
       counter_1_q, multiplexer_1_out, multiplexer_2_out, multiplexer_3_out, multiplexer_4_out,
       multiplexer_5_out, multiplexer_6_out;

  DotMatrix #(.matrixcols(2), .matrixrows(3)) dotmatrix_1 (.col0(in_13), .col1(in_16));
  Multiplexer #(.width(8)) multiplexer_1 (
    .in0(in_1), .in1(_1000), .out(multiplexer_1_out), .sel(in_13[2]));  // open: en
  Counter counter_1 (
    .load(\_1_grava_0_lê ), .D(in_17), .count(_1_acrescenta), .Q(counter_1_q), .clk(in_19),
    .clr(controlled_inverter_1_out));  // open: carry
  assign controlled_buffer_1_out = in_15 ? adder_5_out : 8'bz;  // Controlled_Buffer controlled_buffer_1
  assign controlled_inverter_1_out = volta_para_o_0 ? ~in_15 : 1'bz;  // Controlled_Inverter controlled_inverter_1
  Multiplexer #(.width(8)) multiplexer_2 (.in0(in_2), .in1(in_8), .out(multiplexer_2_out), .sel(in_13[1]));  // open: en
  not not_1 (not_1_out, in_15);
  Adder adder_1 (.a(multiplexer_2_out), .b(multiplexer_1_out), .out(adder_1_out));  // open: cin, cout
  RAM #(.bus("asynch")) ram_1 (.addr(counter_1_q), .data(controlled_buffer_1_out), .ld(not_1_out));  // open: sel, clr
  Multiplexer #(.width(8)) multiplexer_3 (.in0(in_3), .in1(_100), .out(multiplexer_3_out), .sel(in_13[0]));  // open: en
  Adder adder_2 (.a(multiplexer_3_out), .b(adder_1_out), .out(adder_2_out));  // open: cin, cout
  Multiplexer #(.width(8)) multiplexer_4 (
    .in0(in_4), .in1(_1001), .out(multiplexer_4_out), .sel(in_16[2]));  // open: en
  ROM #(.dataWidth(7)) rom_1 (.addr(controlled_buffer_1_out), .data(rom_1_data), .sel(in_19));
  Adder adder_3 (.a(multiplexer_4_out), .b(adder_2_out), .out(adder_3_out));  // open: cin, cout
  TTY tty_1 (.data(rom_1_data), .clk(in_19), .we(in_21));  // open: clr
  Multiplexer #(.width(8)) multiplexer_5 (.in0(in_5), .in1(_110), .out(multiplexer_5_out), .sel(in_16[1]));  // open: en
  Adder adder_4 (.a(multiplexer_5_out), .b(adder_3_out), .out(adder_4_out));  // open: cin, cout
  Multiplexer #(.width(8)) multiplexer_6 (
    .in0(in_6), .in1(_1101), .out(multiplexer_6_out), .sel(in_16[0]));  // open: en
  Adder adder_5 (.a(multiplexer_6_out), .b(adder_4_out), .out(adder_5_out));  // open: cin, cout

  // Notes on the sheet:
  //   111
endmodule
